// Logisim project BullsAndCows.circ as structural Verilog
module main (
);

  wire _0_out, _1_out, _2_out, _3_out, _4_out, _5_out, _6_out, _7_out, _8_out, _9_out, button_2_out,
       button_out, Clock, decoder_1_out0, decoder_1_out1, decoder_1_out2, decoder_1_out3, Enter_out,
       not_1_out, undriven_2, undriven_5, undriven_6, undriven_7;
  wire [1:0] Digit_Selector;
  wire [3:0] number_display_d0, number_display_d1, number_display_d2, number_display_d3, undriven,
       undriven_3, undriven_4, undriven_8;

  Button _1 (.out(_1_out));
  Button _4 (.out(_4_out));
  Button _7 (.out(_7_out));
  Button button (.out(button_out));
  Clock clock_1 (.out(Clock));
  Button _2 (.out(_2_out));
  Button _3 (.out(_3_out));
  Button _5 (.out(_5_out));
  Button _6 (.out(_6_out));
  Button _8 (.out(_8_out));
  Button _9 (.out(_9_out));
  Button _0 (.out(_0_out));
  Button button_2 (.out(button_2_out));
  Button Enter (.out(Enter_out));
  digit_selector u_digit_selector (.L(button_out), .R(button_2_out), .Clock(Clock), .Digit_Place(Digit_Selector));
  number_display number_display (
    ._0(_0_out), ._1(_1_out), ._2(_2_out), ._3(_3_out), ._4(_4_out), ._5(_5_out), ._6(_6_out), ._7(_7_out),
    ._8(_8_out), ._9(_9_out), .Clock(Clock), .Digit_Place(Digit_Selector), .D0(number_display_d0),
    .D1(number_display_d1), .D2(number_display_d2), .D3(number_display_d3));
  Decoder #(.select(2)) decoder_1 (
    .out0(decoder_1_out0), .out1(decoder_1_out1), .out2(decoder_1_out2), .out3(decoder_1_out3),
    .sel(Digit_Selector));  // open: en
  LED led_1 (.in(decoder_1_out3));
  Hex_Digit_Display hex_digit_display_1 (.value(number_display_d3));  // open: dp
  Hex_Digit_Display hex_digit_display_2 (.value(undriven));  // open: dp
  not not_1 (not_1_out, undriven_2);
  Hex_Digit_Display hex_digit_display_3 (.value(undriven_3));  // open: dp
  Hex_Digit_Display hex_digit_display_4 (.value(undriven_4));  // open: dp
  LED led_2 (.in(decoder_1_out2));
  Hex_Digit_Display hex_digit_display_5 (.value(number_display_d2));  // open: dp
  Hex_Digit_Display hex_digit_display_6 (.value(undriven_8));  // open: dp
  LED Win (.in(undriven_2));
  LED Lose (.in(not_1_out));
  LED Start (.in(undriven_5));
  LED Game (.in(undriven_6));
  LED Wait (.in(undriven_7));
  LED led_3 (.in(decoder_1_out0));
  LED led_4 (.in(decoder_1_out1));
  Hex_Digit_Display hex_digit_display_7 (.value(number_display_d1));  // open: dp
  Hex_Digit_Display hex_digit_display_8 (.value(number_display_d0));  // open: dp

  // Notes on the sheet:
  //   Inputs
  //   INSERT CIRCUIT HERE
  //   Bulls
  //   Outputs
  //   Lives
  //   Wins
  //   Cows
endmodule

module game_state_controller (
);

  wire [3:0] overwrite_register_1_data_read, undriven;

  // Probe on undriven
  // Probe on overwrite_register_1_data_read
  overwrite_register overwrite_register_1 (
    .Data_Write(undriven), .Data_Read(overwrite_register_1_data_read));  // open: Clock, Overwrite
endmodule

module memory_unit (
  input  [3:0] D0,
  input  [3:0] D1,
  input  [3:0] D2,
  input  [3:0] D3,
  input  [2:0] Game_State,
  input  Enter_Pressed,
  input  Clock,
  output [3:0] S0,
  output [3:0] S1,
  output [3:0] S2,
  output [3:0] S3,
  output [3:0] G0,
  output [3:0] G1,
  output [3:0] G2,
  output [3:0] G3
);

  overwrite_register overwrite_register_1 (.Data_Write(D3), .Clock(Clock), .Data_Read(S3));  // open: Overwrite
  overwrite_register overwrite_register_2 (.Data_Write(D3), .Clock(Clock), .Data_Read(G3));  // open: Overwrite
  overwrite_register overwrite_register_3 (.Data_Write(D2), .Clock(Clock), .Data_Read(S2));  // open: Overwrite
  overwrite_register overwrite_register_4 (.Data_Write(D2), .Clock(Clock), .Data_Read(G2));  // open: Overwrite
  overwrite_register overwrite_register_5 (.Data_Write(D1), .Clock(Clock), .Data_Read(S1));  // open: Overwrite
  overwrite_register overwrite_register_6 (.Data_Write(D1), .Clock(Clock), .Data_Read(G1));  // open: Overwrite
  overwrite_register overwrite_register_7 (.Data_Write(D0), .Clock(Clock), .Data_Read(S0));  // open: Overwrite
  overwrite_register overwrite_register_8 (.Data_Write(D0), .Clock(Clock), .Data_Read(G0));  // open: Overwrite
endmodule

module sandbox (
  input  A3,
  input  A2,
  input  A1,
  input  A0
);

  wire n7_segment_display_driver_1_p5, n7_segment_display_driver_1_p6, n7_segment_display_driver_1_p7,
       n7_segment_display_driver_1_p8, n7_segment_display_driver_1_p9, n7_segment_display_driver_1_p10,
       n7_segment_display_driver_1_p11;

  Hex_Digit_Display hex_digit_display_1 (.value({A3, A2, A1, A0}));  // open: dp
  // _7_segment_display_driver 7_segment_display_driver_1: pin names not known; wires that end beside it: A3, A2, A1, A0, n7_segment_display_driver_1_p5, n7_segment_display_driver_1_p6, n7_segment_display_driver_1_p7, n7_segment_display_driver_1_p8, n7_segment_display_driver_1_p9, n7_segment_display_driver_1_p10, n7_segment_display_driver_1_p11
  _7_Segment_Display u_7_segment_display_1 (
    .g(n7_segment_display_driver_1_p11), .f(n7_segment_display_driver_1_p10),
    .a(n7_segment_display_driver_1_p5), .b(n7_segment_display_driver_1_p6),
    .e(n7_segment_display_driver_1_p9), .d(n7_segment_display_driver_1_p8), .c(n7_segment_display_driver_1_p7));  // open: dp

  // Notes on the sheet:
  //   Hex Digit Display
  //   Inputs
  //   7-Segment + Decoder
endmodule

module overwrite_register (
  input  [3:0] Data_Write,
  input  Clock,
  input  Overwrite,
  output [3:0] Data_Read
);

  wire [3:0] controlled_buffer_1_out;

  assign controlled_buffer_1_out = Overwrite ? Data_Write : 4'bz;  // Controlled_Buffer controlled_buffer_1
  Register #(.width(4)) register_1 (.D(controlled_buffer_1_out), .Q(Data_Read), .clk(Clock));  // open: en, clr
endmodule

module digit_selector (
  input  L,
  input  R,
  input  Clock,
  output [1:0] Digit_Place
);

  wire and_1_out, and_2_out, and_3_out, and_4_out, and_5_out, and_6_out, and_7_out, and_8_out, and_9_out,
       not_1_out, not_2_out, not_3_out, not_4_out, not_5_out, not_6_out, not_7_out, not_8_out, not_9_out,
       not_10_out, not_11_out, not_12_out, not_13_out, not_14_out, or_1_out, or_2_out;

  not not_1 (not_1_out, R);
  not not_2 (not_2_out, L);
  not not_3 (not_3_out, R);
  not not_4 (not_4_out, Digit_Place[1]);
  not not_5 (not_5_out, Digit_Place[0]);
  not not_6 (not_6_out, L);
  not not_7 (not_7_out, Digit_Place[1]);
  not not_8 (not_8_out, Digit_Place[0]);
  not not_9 (not_9_out, R);
  and and_1 (and_1_out, not_9_out, not_10_out, Digit_Place[0]);
  not not_10 (not_10_out, L);
  not not_11 (not_11_out, R);
  and and_2 (and_2_out, not_11_out, L, not_12_out);
  not not_12 (not_12_out, Digit_Place[0]);
  and and_3 (and_3_out, R, not_13_out, not_14_out);
  not not_13 (not_13_out, L);
  not not_14 (not_14_out, Digit_Place[0]);
  and and_4 (and_4_out, R, L, Digit_Place[0]);
  and and_5 (and_5_out, not_1_out, not_2_out, Digit_Place[1]);
  and and_6 (and_6_out, not_3_out, L, not_4_out, Digit_Place[0]);
  and and_7 (and_7_out, L, Digit_Place[1], not_5_out);
  and and_8 (and_8_out, R, not_6_out, not_7_out, not_8_out);
  and and_9 (and_9_out, R, Digit_Place[1], Digit_Place[0]);
  or or_1 (or_1_out, and_1_out, and_2_out, and_3_out, and_4_out);
  or or_2 (or_2_out, and_5_out, and_6_out, and_7_out, and_8_out, and_9_out);
  D_Flip_Flop d_ff_1 (.clk(Clock), .D(or_2_out), .Q(Digit_Place[1]));  // open: Qn, preset, en, reset
  D_Flip_Flop d_ff_2 (.clk(Clock), .D(or_1_out), .Q(Digit_Place[0]));  // open: Qn, preset, en, reset
endmodule

module number_display (
  input  _0,
  input  _1,
  input  _2,
  input  _3,
  input  _4,
  input  _5,
  input  _6,
  input  _7,
  input  _8,
  input  _9,
  input  Clock,
  input  [1:0] Digit_Place,
  output [3:0] D0,
  output [3:0] D1,
  output [3:0] D2,
  output [3:0] D3
);

  wire and_1_out, and_2_out, and_3_out, and_4_out, decoder_1_out0, decoder_1_out1, decoder_1_out2,
       decoder_1_out3, priority_encoder_1_gs;
  wire [3:0] priority_encoder_1_out;

  Priority_Encoder #(.select(4)) priority_encoder_1 (
    .in0(_0), .in1(_1), .in2(_2), .in3(_3), .in4(_4), .in5(_5), .in6(_6), .in7(_7), .in8(_8), .in9(_9),
    .out(priority_encoder_1_out), .gs(priority_encoder_1_gs));  // open: in10, in11, in12, in13, in14, in15, en_out, en_in
  // Probe on priority_encoder_1_out
  overwrite_register overwrite_register_1 (
    .Data_Write(priority_encoder_1_out), .Clock(Clock), .Overwrite(and_1_out), .Data_Read(D0));
  overwrite_register overwrite_register_2 (
    .Data_Write(priority_encoder_1_out), .Clock(Clock), .Overwrite(and_2_out), .Data_Read(D1));
  overwrite_register overwrite_register_3 (
    .Data_Write(priority_encoder_1_out), .Clock(Clock), .Overwrite(and_3_out), .Data_Read(D2));
  overwrite_register overwrite_register_4 (
    .Data_Write(priority_encoder_1_out), .Clock(Clock), .Overwrite(and_4_out), .Data_Read(D3));
  Decoder #(.select(2)) decoder_1 (
    .out0(decoder_1_out0), .out1(decoder_1_out1), .out2(decoder_1_out2), .out3(decoder_1_out3),
    .sel(Digit_Place));  // open: en
  and and_1 (and_1_out, priority_encoder_1_gs, decoder_1_out0);
  and and_2 (and_2_out, priority_encoder_1_gs, decoder_1_out1);
  and and_3 (and_3_out, priority_encoder_1_gs, decoder_1_out2);
  and and_4 (and_4_out, priority_encoder_1_gs, decoder_1_out3);

  // Other names for the same wires on the sheet: Clock_T = Clock
endmodule
